# Fritzing sketch PowerMonitor_Schematics (saved by Fritzing 0.9.3b)
breadboards: 1

parts:
  Arduino_Nano = Arduino Nano (Rev3.0)
  INA219 = Adafruit INA219 High Side DC Current Sensor Breakout [part_number="Adafruit #904"]
  J1 = male pin header, 2 pins [form="♂ (male)"]

nets:
  GND: Arduino_Nano.GND, INA219.GND
  5V: Arduino_Nano.5V, INA219.VCC
  N1: Arduino_Nano.A5, INA219.SCL
  N2: Arduino_Nano.A4, INA219.SDA
  N3: INA219.VIN-, J1.pin1
  N4: INA219.VIN+, J1.pin2

custom parts:
  Adafruit INA219 High Side DC Current Sensor Breakout: This breakout board will solve all your power-monitoring problems. Instead of struggling with two multimeters, you can just use the handy INA219B chip on this breakout to both measure both the high side voltage and DC current draw over I2C with 1% precision. Most current-measuring devices such as our current panel meter are only good for low side measuring. That means that unless you want to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
