# Fritzing sketch PowerMonitor_Schematics_with_LCD (saved by Fritzing 0.9.3b)
breadboards: 2

parts:
  Arduino_Nano = Arduino Nano (Rev3.0)
  INA219_current_sensor = Adafruit INA219 High Side DC Current Sensor Breakout [part_number="Adafruit #904"]
  J1 = male pin header, 2 pins [form="♂ (male)"]
  LCD1 = LCD screen
  R1 = Trimmer Potentiometer [maximum_resistance=10kΩ package=THT]

nets:
  GND: Arduino_Nano.GND, INA219_current_sensor.GND, LCD1.VSS, LCD1.R/W, R1.leg2
  N1: Arduino_Nano.D2, LCD1.DB7
  N2: Arduino_Nano.D3, LCD1.DB6
  N3: Arduino_Nano.D4, LCD1.DB5
  N4: Arduino_Nano.D5, LCD1.DB4
  N5: Arduino_Nano.D11/MOSI, LCD1.E
  N6: Arduino_Nano.D12/MISO, LCD1.RS
  5V: Arduino_Nano.5V, INA219_current_sensor.VCC, LCD1.VDD, R1.leg1
  N7: Arduino_Nano.A5, INA219_current_sensor.SCL
  N8: Arduino_Nano.A4, INA219_current_sensor.SDA
  N9: INA219_current_sensor.VIN-, J1.pin1
  N10: INA219_current_sensor.VIN+, J1.pin2
  N11: LCD1.V0, R1.wiper

custom parts:
  Adafruit INA219 High Side DC Current Sensor Breakout: This breakout board will solve all your power-monitoring problems. Instead of struggling with two multimeters, you can just use the handy INA219B chip on this breakout to both measure both the high side voltage and DC current draw over I2C with 1% precision. Most current-measuring devices such as our current panel meter are only good for low side measuring. That means that unless you want to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
